# Fritzing sketch circuit (saved by Fritzing 1.0.5)
breadboards: 1

parts:
  A1 = Arduino UNO R4 WiFi
  R4 = 6mm Trimmer Potentiometer [maximum_resistance=10kΩ knob_status=50% power=0.5W package=THT]

nets:
  N1: A1.Pin_2, A1.Pin_25, R4.leg2
  N2: A1.Pin_8, A1.Pin_27, R4.leg1
  N3: A1.Pin_12, R4.wiper

custom parts:
  Arduino UNO R4 WiFi: The Arduino UNO R4 WiFi merges the RA4M1 microprocessor from Renesas with the ESP32-S3 from Espressif, creating an all-in-one tool for makers with enhanced processing power and a diverse array of new peripherals.
